# Fritzing sketch CatDogToy Fritzing (saved by Fritzing 1.0.0rc)
breadboards: 1

parts:
  A1 = Particle - Photon2
  HC-SR04_Sensor_1 = HC-SR04 Ultrasonic Distance Sensor
  Mod1 = Passive Buzzer
  S1 = Pushbutton [package="[THT]"]
  LED1 = LED - 3mm [color="Red (633nm)" current=0.030A package="3 mm [THT]"]
  LED2 = LED - 3mm [color="Red (633nm)" current=0.030A package="3 mm [THT]"]
  R1 = Resistor [tolerance=±5% power=0.25W resistance=220 package=THT]
  OLED_I2C1 = OLED 128x64 I2C Monochrome Display

nets:
  N1: A1.Pin_2, A1.Pin_31, HC-SR04_Sensor_1.VCC
  N2: A1.Pin_12, Mod1.S
  N3: A1.Pin_13, HC-SR04_Sensor_1.ECHO
  N4: A1.Pin_17, OLED_I2C1.SDA
  N5: A1.Pin_18, OLED_I2C1.SCK
  GND: A1.Pin_19, HC-SR04_Sensor_1.GND, Mod1.-, S1.Pin_3, S1.Pin_4, OLED_I2C1.GND
  N6: A1.Pin_21, HC-SR04_Sensor_1.TRIG
  N7: A1.Pin_23, LED1.anode, LED2.anode
  N8: Mod1.NC, S1.Pin_1, S1.Pin_2, OLED_I2C1.VDD
  N9: LED1.cathode, LED2.cathode, R1.Pin_1

custom parts:
  Particle - Photon2: The Photon 2 is a microcontroller and Wi-Fi networking developed by particle. Features: 802.11a/b/g/n Wi-Fi, 2.4 GHz and 5 GHz Integrated PCB antenna Integrated U.FL connector for external antenna Integrated RF switch BLE 5 using same antenna as Wi-Fi Realtek RTL8721DM MCU ARM Cortex M33 CPU, 200 MHz 2048 KB (2 MB) user application maximum size 3072 KB (3 MB) of RAM available to user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
  Pushbutton: A generic pushbutton.
